// Digital circuit CPU 4.dig as structural Verilog
module CPU_4 (
  input  clk,
  output CLK1,
  output CLK2
);

  wire _74245_1_p13, _74245_1_p14, _74245_1_p15, _74245_1_p16, _74245_1_p17, _74245_1_p18, _74245_1_p19,
       _74245_1_p20, and_1_out, and_2_out, and_3_out, and_6_out, and_7_out, and_8_out, and_9_out,
       bussplitter_1_d0, bussplitter_1_d1, bussplitter_1_d2, bussplitter_1_d3, bussplitter_1_d4,
       bussplitter_1_d5, bussplitter_1_d6, bussplitter_1_d7, CARRY, d_ff_as_1_q, d_ff_as_3_q,
       demultiplexer_1_out_1, demultiplexer_1_out_2, demultiplexer_1_out_3, demultiplexer_1_out_4,
       demultiplexer_2_out_1, demultiplexer_2_out_2, demultiplexer_2_out_3, demultiplexer_2_out_4,
       demultiplexer_2_out_5, demultiplexer_2_out_6, demultiplexer_2_out_7, demultiplexer_3_out_1,
       demultiplexer_3_out_2, demultiplexer_3_out_3, EQUAL, FP_INC, FP_JMP, FP_JMP0, FP_RUN, FP_STEP,
       FP_STEP0, HALT, JMP_C, JMP_E, JMP_EN, JMP_POS, multiplexer_2_out, nA_DOUT, nA_ST, nDISP_ST, nMAR_ST,
       nMEM_DOUT, nMEM_ST, nOP_ST, not_10_out, not_12_out, not_13_out, not_14_out, not_16_out, not_17_out,
       not_18_out, not_19_out, not_20_out, not_21_out, not_22_out, nPC_ST, nROM_DOUT, nSUM_DOUT, nSUM_ST,
       or_1_out, or_3_out, or_5_out, t_ff_1_nq, t_ff_1_q;
  wire [1:0] alu4_1_p7, JMP_SEL;
  wire [2:0] DOUT, ST;
  wire [3:0] H_d, H_d_2, O_d, T_d, T_d_2;
  wire [7:0] A_q, alu4_1_p5, d_ff_1_q, d_ff_1_q_2, d_ff_2_q, d_ff_3_q, DATA, dipswitch_8_out, DISP_q, MAR_q,
       MEM__128x8_d, OP_q, PC_out, SUM_q;
  wire [7:4] O_d_2;
  wire [15:0] CTRL_q, IWORD;

  LED BR1 (.in(d_ff_1_q_2[7]));
  LED BR0 (.in(d_ff_1_q_2[6]));
  and and_1 (and_1_out, nPC_ST, ~FP_JMP);  // And
  Demultiplexer #(.Selector_Bits(3)) demultiplexer_1 (
    .sel(DOUT), .in(1'b1), .out_1(demultiplexer_1_out_1), .out_2(demultiplexer_1_out_2),
    .out_3(demultiplexer_1_out_3), .out_4(demultiplexer_1_out_4));  // open: out_0, out_5, out_6, out_7
  LED ST2 (.in(d_ff_1_q_2[5]));
  LED ST1 (.in(d_ff_1_q_2[4]));
  not not_1 (nA_DOUT, demultiplexer_1_out_1);
  not not_2 (nMEM_DOUT, demultiplexer_1_out_2);
  not not_3 (nSUM_DOUT, demultiplexer_1_out_3);
  not not_4 (nROM_DOUT, demultiplexer_1_out_4);
  LED ST0 (.in(d_ff_1_q_2[3]));
  LED DT2 (.in(d_ff_1_q_2[2]));
  CounterPreset #(.Bits(8)) PC (
    .en(~FP_JMP), .C(CLK2), .dir(1'b0), .in(DATA), .ld(~and_1_out), .clr(1'b0), .out(PC_out));  // open: ovf
  LED DT1 (.in(d_ff_1_q_2[1]));
  LED DT0 (.in(d_ff_1_q_2[0]));
  and and_2 (and_2_out, ~JMP_C, ~CARRY);  // And
  and and_3 (and_3_out, ~JMP_E, EQUAL);  // And
  LED IM7 (.in(d_ff_1_q[7]));
  LED IM6 (.in(d_ff_1_q[6]));
  DipSwitch dipswitch_1 (.out(dipswitch_8_out[7]));
  DipSwitch dipswitch_2 (.out(dipswitch_8_out[6]));
  ROM #(.AddrBits(8), .Bits(16)) rom_1 (.A(PC_out), .sel(1'b1), .D(IWORD));
  or or_1 (or_1_out, and_2_out, and_3_out);
  Demultiplexer #(.Selector_Bits(3)) demultiplexer_2 (
    .sel(ST), .in(1'b1), .out_1(demultiplexer_2_out_1), .out_2(demultiplexer_2_out_2),
    .out_3(demultiplexer_2_out_3), .out_4(demultiplexer_2_out_4), .out_5(demultiplexer_2_out_5),
    .out_6(demultiplexer_2_out_6), .out_7(demultiplexer_2_out_7));  // open: out_0
  LED IM5 (.in(d_ff_1_q[5]));
  LED IM4 (.in(d_ff_1_q[4]));
  DipSwitch dipswitch_3 (.out(dipswitch_8_out[5]));
  DipSwitch dipswitch_4 (.out(dipswitch_8_out[4]));
  D_FF #(.Bits(16)) CTRL (.D(IWORD), .C(CLK1), .Q(CTRL_q));  // open: nQ
  not not_5 (nA_ST, demultiplexer_2_out_1);
  not not_6 (nMEM_ST, demultiplexer_2_out_2);
  not not_7 (nSUM_ST, demultiplexer_2_out_3);
  not not_8 (nMAR_ST, demultiplexer_2_out_4);
  not not_9 (nOP_ST, demultiplexer_2_out_5);
  not not_10 (not_10_out, demultiplexer_2_out_6);
  not not_11 (nDISP_ST, demultiplexer_2_out_7);
  LED IM3 (.in(d_ff_1_q[3]));
  LED IM2 (.in(d_ff_1_q[2]));
  DipSwitch dipswitch_5 (.out(dipswitch_8_out[3]));
  DipSwitch dipswitch_6 (.out(dipswitch_8_out[2]));
  not not_12 (not_12_out, or_1_out);
  or or_2 (nPC_ST, not_10_out, JMP_EN);
  LED IM1 (.in(d_ff_1_q[1]));
  LED IM0 (.in(d_ff_1_q[0]));
  DipSwitch dipswitch_7 (.out(dipswitch_8_out[1]));
  DipSwitch dipswitch_8 (.out(dipswitch_8_out[0]));
  assign {JMP_SEL, ST, DOUT} = ~HALT ? CTRL_q[15:8] : 8'bz;  // DriverInvSel driverinvsel_1
  Multiplexer multiplexer_1 (.sel(not_13_out), .in_0(or_1_out), .in_1(not_12_out), .out(JMP_EN));
  D_FF #(.Bits(16)) d_ff_1 (.D(IWORD), .C(~CLK2), .Q({d_ff_1_q_2, d_ff_1_q}));  // open: nQ
  PullDown #(.Bits(8)) pulldown_1 (.out({JMP_SEL, ST, DOUT}));
  not not_13 (not_13_out, JMP_POS);
  not not_14 (not_14_out, FP_JMP);
  assign DATA = ~not_14_out ? dipswitch_8_out : 8'bz;  // DriverInvSel driverinvsel_2
  assign DATA = ~nROM_DOUT ? CTRL_q[7:0] : 8'bz;  // DriverInvSel driverinvsel_3
  Demultiplexer #(.Selector_Bits(2)) demultiplexer_3 (
    .sel(JMP_SEL), .in(1'b1), .out_1(demultiplexer_3_out_1), .out_2(demultiplexer_3_out_2),
    .out_3(demultiplexer_3_out_3));  // open: out_0
  LED D7 (.in(d_ff_2_q[7]));
  LED D6 (.in(d_ff_2_q[6]));
  PullDown pulldown_2 (.out(FP_RUN));
  DipSwitch RUN (.out(FP_RUN));
  DipSwitch STEP (.out(FP_STEP0));
  not not_15 (JMP_C, demultiplexer_3_out_1);
  not not_16 (not_16_out, demultiplexer_3_out_2);
  not not_17 (not_17_out, demultiplexer_3_out_3);
  LED D5 (.in(d_ff_2_q[5]));
  LED D4 (.in(d_ff_2_q[4]));
  PullDown pulldown_3 (.out(FP_JMP0));
  PullDown pulldown_4 (.out(FP_STEP0));
  DipSwitch JMP (.out(FP_JMP0));
  DipSwitch INC (.out(FP_INC));
  and and_4 (JMP_POS, not_16_out, JMP_C);
  LED D3 (.in(d_ff_2_q[3]));
  LED D2 (.in(d_ff_2_q[2]));
  PullDown pulldown_5 (.out(FP_INC));
  and and_5 (JMP_E, not_17_out, not_16_out);
  LED D1 (.in(d_ff_2_q[1]));
  LED D0 (.in(d_ff_2_q[0]));
  D_FF #(.Bits(8)) d_ff_2 (.D(DATA), .C(~CLK2), .Q(d_ff_2_q));  // open: nQ
  and and_6 (and_6_out, FP_JMP0, ~FP_RUN);  // And
  D_FF_AS d_ff_as_1 (.Set(1'b0), .D(FP_STEP), .C(~CLK1), .Clr(~FP_STEP), .Q(d_ff_as_1_q));  // open: nQ
  PullDown #(.Bits(8)) pulldown_6 (.out(DATA));
  not not_18 (not_18_out, OP_q[6]);
  Seven_Seg seven_seg_1 (
    .a(H_d[0]), .b(H_d[1]), .c(H_d[2]), .d(H_d[3]), .e(H_d_2[0]), .f(H_d_2[1]), .g(H_d_2[2]), .dp(H_d_2[3]));
  Register #(.Bits(8)) A (.D(DATA), .C(CLK2), .en(~nA_ST), .Q(A_q));
  Register #(.Bits(8)) OP (.D(DATA), .C(CLK2), .en(~nOP_ST), .Q(OP_q));
  Multiplexer multiplexer_2 (.sel(OP_q[7]), .in_0(not_18_out), .in_1(CARRY), .out(multiplexer_2_out));
  Register #(.Bits(8)) MAR (.D(DATA), .C(CLK2), .en(~nMAR_ST), .Q(MAR_q));
  Seven_Seg seven_seg_2 (
    .a(T_d[0]), .b(T_d[1]), .c(T_d[2]), .d(T_d[3]), .e(T_d_2[0]), .f(T_d_2[1]), .g(T_d_2[2]), .dp(T_d_2[3]));
  and and_7 (and_7_out, FP_STEP, ~d_ff_as_1_q);  // And
  D_FF #(.Bits(8)) d_ff_3 (.D(MAR_q), .C(CLK1), .Q(d_ff_3_q));  // open: nQ
  Seven_Seg seven_seg_3 (
    .a(O_d[0]), .b(O_d[1]), .c(O_d[2]), .d(O_d[3]), .e(O_d_2[4]), .f(O_d_2[5]), .g(O_d_2[6]), .dp(O_d_2[7]));
  D_FF_AS d_ff_as_2 (.Set(and_6_out), .D(1'b0), .C(~CLK2), .Clr(1'b0), .Q(FP_JMP));  // open: nQ
  or or_3 (or_3_out, FP_RUN, and_7_out);
  assign DATA = ~nA_DOUT ? A_q : 8'bz;  // DriverInvSel driverinvsel_4
  or or_4 (FP_STEP, FP_STEP0, FP_JMP, FP_INC);
  and and_8 (and_8_out, or_3_out, ~clk);  // And
  // ALU4 alu4_1: pin names not known; wires that end beside it: A_q, DATA, OP_q[4:0], multiplexer_2_out, alu4_1_p5, alu4_1_p7[1], alu4_1_p7[0]
  or or_5 (or_5_out, 1'b0, d_ff_3_q[7]);
  Register #(.Bits(8)) DISP (.D(DATA), .C(CLK2), .en(~nDISP_ST), .Q(DISP_q));
  ROM #(.AddrBits(8), .Bits(8)) H (.A(DISP_q), .sel(1'b1), .D({H_d_2, H_d}));
  ROM #(.AddrBits(8), .Bits(8)) T (.A(DISP_q), .sel(1'b1), .D({T_d_2, T_d}));
  ROM #(.AddrBits(8), .Bits(8)) O (.A(DISP_q), .sel(1'b1), .D({O_d_2, O_d}));
  D_FF_AS d_ff_as_3 (.Set(and_8_out), .D(1'b0), .C(~CLK2), .Clr(1'b0), .Q(d_ff_as_3_q));  // open: nQ
  Demultiplexer #(.Selector_Bits(3)) demultiplexer_4 (
    .sel(d_ff_3_q[2:0]), .in(d_ff_3_q[7]));  // open: out_0, out_1, out_2, out_3, out_4, out_5, out_6, out_7
  not not_19 (not_19_out, d_ff_as_3_q);
  RAMSinglePortSel #(.AddrBits(7), .Bits(8)) MEM__128x8 (
    .A(d_ff_3_q[6:0]), .CS(~or_5_out), .WE(~nMEM_ST), .OE(~nMEM_DOUT), .D(MEM__128x8_d));
  and and_9 (and_9_out, clk, d_ff_as_3_q);
  or or_6 (HALT, FP_JMP, FP_INC, not_19_out);
  PullDown #(.Bits(8)) pulldown_7 (.out(MEM__128x8_d));
  BusSplitter #(.Bits(8)) bussplitter_1 (
    .D(MEM__128x8_d), .OE(not_20_out), .D0(bussplitter_1_d0), .D1(bussplitter_1_d1), .D2(bussplitter_1_d2),
    .D3(bussplitter_1_d3), .D4(bussplitter_1_d4), .D5(bussplitter_1_d5), .D6(bussplitter_1_d6),
    .D7(bussplitter_1_d7));
  not not_20 (not_20_out, nMEM_DOUT);
  not not_21 (not_21_out, nMEM_DOUT);
  PullDown pulldown_8 (.out(and_9_out));
  not not_22 (not_22_out, and_9_out);
  // _74245 _74245_1: pin names not known; wires that end beside it: not_21_out, 1'b1, 1'b0, bussplitter_1_d0, bussplitter_1_d1, bussplitter_1_d2, bussplitter_1_d3, bussplitter_1_d4, bussplitter_1_d5, bussplitter_1_d6, bussplitter_1_d7, 1'b0, _74245_1_p13, _74245_1_p14, _74245_1_p15, _74245_1_p16, _74245_1_p17, _74245_1_p18, _74245_1_p19, _74245_1_p20
  T_FF #(.withEnable("false")) t_ff_1 (.C(not_22_out), .Q(t_ff_1_q), .nQ(t_ff_1_nq));
  and and_10 (CLK1, and_9_out, t_ff_1_q);
  and and_11 (CLK2, t_ff_1_nq, and_9_out);
  Register #(.Bits(2)) CE (.D(alu4_1_p7), .C(CLK2), .en(~nSUM_ST), .Q({EQUAL, CARRY}));
  Register #(.Bits(8)) SUM (.D(alu4_1_p5), .C(CLK2), .en(~nSUM_ST), .Q(SUM_q));
  PullDown pulldown_9 (.out(_74245_1_p20));
  PullDown pulldown_10 (.out(_74245_1_p19));
  PullDown pulldown_11 (.out(_74245_1_p18));
  PullDown pulldown_12 (.out(_74245_1_p17));
  PullDown pulldown_13 (.out(_74245_1_p16));
  assign DATA = ~nSUM_DOUT ? SUM_q : 8'bz;  // DriverInvSel driverinvsel_5
  BusSplitter #(.Bits(8)) bussplitter_2 (
    .D(DATA), .OE(nMEM_DOUT), .D0(_74245_1_p13), .D1(_74245_1_p14), .D2(_74245_1_p15), .D3(_74245_1_p16),
    .D4(_74245_1_p17), .D5(_74245_1_p18), .D6(_74245_1_p19), .D7(_74245_1_p20));
  PullDown pulldown_14 (.out(_74245_1_p15));
  PullDown pulldown_15 (.out(_74245_1_p14));
  PullDown pulldown_16 (.out(_74245_1_p13));

  // Other names for the same wires on the sheet: CLK_1 = CLK1; CLK_2 = CLK2

  // Notes on the sheet:
  //   clk: Hz: 10
  //   PANEL0
  //   ATLAS PDC-8
  //   CTRL0
  //   CTRL1
  //   contents of rom_1 (hex, n*v repeats v):
  //   2c09,1800,2400,c01,1401,7400,3900,1a00,1300,7400,3a00,1a00,b00,3405
  //   PANEL2
  //   PANEL1
  //   ALU
  //   MEM
  //   contents of H (hex, n*v repeats v):
  //   100*0,100*6,56*5b
  //   contents of T (hex, n*v repeats v):
  //   10*0,10*6,10*5b,10*4f,10*66,10*6d,10*7d,10*7,10*7f,10*6f,10*3f
  //   ,10*6,10*5b,10*4f,10*66,10*6d,10*7d,10*7,10*7f,10*6f,10*3f,10*6
  //   ,10*5b,10*4f,10*66,6*6d
  //   contents of O (hex, n*v repeats v):
  //   3f,6,5b,4f,66,6d,7d,7,7f,6f,3f,6,5b,4f,66,6d,7d,7,7f,6f,3f,6,5b
  //   ,4f,66,6d,7d,7,7f,6f,3f,6,5b,4f,66,6d,7d,7,7f,6f,3f,6,5b,4f,66
  //   ,6d,7d,7,7f,6f,3f,6,5b,4f,66,6d,7d,7,7f,6f,3f,6,5b,4f,66,6d,7d
  //   ,7,7f,6f,3f,6,5b,4f,66,6d,7d,7,7f,6f,3f,6,5b,4f,66,6d,7d,7,7f
  //   ,6f,3f,6,5b,4f,66,6d,7d,7,7f,6f,3f,6,5b,4f,66,6d,7d,7,7f,6f,3f
  //   ,6,5b,4f,66,6d,7d,7,7f,6f,3f,6,5b,4f,66,6d,7d,7,7f,6f,3f,6,5b
  //   ,4f,66,6d,7d,7,7f,6f,3f,6,5b,4f,66,6d,7d,7,7f,6f,3f,6,5b,4f,66
  //   ,6d,7d,7,7f,6f,3f,6,5b,4f,66,6d,7d,7,7f,6f,3f,6,5b,4f,66,6d,7d
  //   ,7,7f,6f,3f,6,5b,4f,66,6d,7d,7,7f,6f,3f,6,5b,4f,66,6d,7d,7,7f
  //   ,6f,3f,6,5b,4f,66,6d,7d,7,7f,6f,3f,6,5b,4f,66,6d,7d,7,7f,6f,3f
  //   ,6,5b,4f,66,6d,7d,7,7f,6f,3f,6,5b,4f,66,6d,7d,7,7f,6f,3f,6,5b
  //   ,4f,66,6d,7d,7,7f,6f,3f,6,5b,4f,66,6d
endmodule
